# Fritzing sketch FSR (saved by Fritzing 0.9.0b)
breadboards: 1

parts:
  J1 = Basic Force Sensing Resistor (FSR) [package=THT]
  Part1 = Arduino Uno (Rev3)
  R1 = Resistor [tolerance=±5% resistance=10k package=THT]

nets:
  N1: J1.pin_0, Part1.5V
  N2: J1.pin_1, Part1.A3, R1.Pin_1
  N3: Part1.GND, R1.Pin_0
