# Fritzing sketch hc-05-serial (saved by Fritzing 0.9.0b)

parts:
  Part1 = Bluetooth HC-05 Macho
  Part2 = Arduino Uno (Rev3)

nets:
  N1: Part1.TXD, Part2.D2
  N2: Part1.RXD, Part2.D3_PWM
  VCC: Part1.VCC, Part2.3V3
  GND: Part1.GND, Part2.GND
