# Fritzing sketch sign language circuit (saved by Fritzing 0.9.0b)
breadboards: 1

parts:
  R1 = Resistor [tolerance=±5% resistance=10k package=THT]
  Part1 = Arduino Nano (Rev3.0)
  R2 = Resistor [tolerance=±5% resistance=10k package=THT]
  R3 = Resistor [tolerance=±5% resistance=10k package=THT]
  R4 = Resistor [tolerance=±5% resistance=10k package=THT]
  R5 = Resistor [tolerance=±5% resistance=10k package=THT]
  R6 = Basic Flex Resistor
  R7 = Basic Flex Resistor
  R8 = Basic Flex Resistor
  J1 = Basic Force Sensing Resistor (FSR) [package=THT]
  J2 = Basic Force Sensing Resistor (FSR) [package=THT]
  Part2 = Bluetooth HC-05 Macho

nets:
  GND: R1.Pin_0, Part1.GND, R2.Pin_0, R3.Pin_0, R4.Pin_0, R5.Pin_0, Part2.GND
  N1: R1.Pin_1, Part1.A0, R6.Pin_2
  N2: Part1.D2, Part2.TXD
  N3: Part1.D3, Part2.RXD
  N4: Part1.5V, R6.pin_1, R7.pin_1, R8.pin_1, J1.pin_0, J2.pin_0
  N5: Part1.A7, R5.Pin_1, J2.pin_1
  N6: Part1.A5, R4.Pin_1, J1.pin_1
  N7: Part1.A3, R3.Pin_1, R7.Pin_2
  N8: Part1.A1, R2.Pin_1, R8.Pin_2
  3V3: Part1.3V3, Part2.VCC
